// Logisim project Lab6.circ as structural Verilog: 3 circuits, main circuit main
module main (
  output [31:0] out_1,
  output [2:0] out_2,
  output [1:0] out_3,
  output [31:0] pc,
  output [6:0] out_5,
  output out_6,
  output [4:0] out_7,
  output [31:0] out_8,
  output [3:0] out_9,
  output [2:0] out_10,
  output out_11,
  output [4:0] out_12,
  output [31:0] Instr,
  output [31:0] out_14,
  output out_15,
  output [4:0] out_16,
  output out_17,
  output [6:0] out_18,
  output out_19,
  output [31:0] out_20,
  output out_21,
  output [31:0] Imm
);

  wire and_1_out, Clk, not_1_out, not_2_out, or_1_out, Reset, ZERO;
  wire [31:0] adder_1_out, multiplexer_1_out, multiplexer_2_out, multiplexer_3_out, ram_1_data, undriven;

  not not_1 (not_1_out, Clk);
  and and_1 (and_1_out, out_15, ZERO);
  or or_1 (or_1_out, and_1_out, out_11);
  _32_32Regfile u_32_32regfile_1 (
    .R1_num(out_12), .R2_num(out_16), .Write_Reg_num(out_7), .Write_Enable(out_21), .Clock(Clk), .Din(out_1),
    .Reg1Out(out_8), .Reg2Out(out_14), .Reset(Reset));
  Button button_1 (.out(Reset));
  Clock clock_1 (.out(Clk));
  Register #(.width(32), .Select("low")) u_PC (.D(adder_1_out), .Q(pc), .clk(not_1_out), .clr(Reset));  // open: en
  Multiplexer #(.width(32), .enable("false")) multiplexer_1 (
    .in0(32'h4), .in1(Imm), .out(multiplexer_1_out), .sel(or_1_out));
  Adder #(.width(32)) adder_1 (.a(pc), .b(multiplexer_1_out), .out(adder_1_out));  // open: cin, cout
  ROM #(.addrWidth(24), .dataWidth(32), .Select("low")) rom_1 (.addr(pc[25:2]), .data(Instr));
  Multiplexer #(.width(32), .enable("false")) multiplexer_2 (
    .in0(out_8), .in1(pc), .out(multiplexer_2_out), .sel(out_6));
  ALU alu_1 (.Zero(ZERO), .Result(out_20), .A(multiplexer_2_out), .B(multiplexer_3_out), .ALUctr(out_9));
  Multiplexer #(.select(2), .width(32), .enable("false")) multiplexer_3 (
    .in0(out_14), .in1(32'h4), .in2(Imm), .in3(undriven), .out(multiplexer_3_out), .sel(out_3));
  \指令解析  \u_指令解析_1  (
    .\输入指令 (Instr), .ExtOp(out_2), .op(out_5), .Rd(out_7), .funct3(out_10), .Rs1(out_12), .Rs2(out_16),
    .funct7(out_18), .Imm(Imm));
  Controller controller_1 (
    .funct3(out_10), .op(out_5), .Branch(out_15), .Jump(out_11), .ALUASrs(out_6), .ALUBSrc(out_3),
    .ALUctr(out_9), .MemtoReg(out_19), .RegWr(out_21), .MemWr(out_17), .ExtOp(out_2));
  not not_2 (not_2_out, Clk);
  RAM #(.addrWidth(24), .dataWidth(32), .bus("separate"), .Select("low")) ram_1 (
    .addr(out_20[25:2]), .din(out_14), .data(ram_1_data), .str(out_17), .clk(not_2_out), .clr(Reset));  // open: sel, ld
  Multiplexer #(.width(32), .enable("false")) multiplexer_4 (.in0(out_20), .in1(ram_1_data), .out(out_1), .sel(out_19));

  // Other names for the same wires on the sheet: ALUASrc = out_6; ALUBSrc[1:0] = out_3; ALUctr[3:0] = out_9;
  //   Branch = out_15; busA[31:0] = out_8; busB[31:0] = out_14; busW[31:0] = out_1; ExtOp[2:0] = out_2;
  //   funct3[2:0] = out_10; funct7[6:0] = out_18; Jump = out_11; MemtoReg = out_19; MemWr = out_17; op[6:0] = out_5;
  //   Rd[4:0] = out_7; RegWr = out_21; Result[31:0] = out_20; Rs1[4:0] = out_12; Rs2[4:0] = out_16

  // Notes on the sheet:
  //   contents of rom_1 (hex, n*v repeats v):
  //   2183 106293 106113 520233 328663 2282b3 ff5ff06f 402223 6f
endmodule

module \指令解析  (
  input  [31:0] \输入指令 ,
  input  [2:0] ExtOp,
  output [31:0] Imm,
  output [6:0] op,
  output [4:0] Rd,
  output [2:0] funct3,
  output [4:0] Rs1,
  output [4:0] Rs2,
  output [6:0] funct7
);

  InstrTolmm instrtolmm_1 (.Instr(\输入指令 ), .Extop(ExtOp), .imm(Imm));

  assign funct3 = \输入指令 [14:12];
  assign funct7 = \输入指令 [31:25];
  assign op = \输入指令 [6:0];
  assign Rd = \输入指令 [11:7];
  assign Rs1 = \输入指令 [19:15];
  assign Rs2 = \输入指令 [24:20];
endmodule

module Controller (
  input  [2:0] funct3,
  input  [6:0] op,
  output Branch,
  output Jump,
  output ALUASrs,
  output [1:0] ALUBSrc,
  output [3:0] ALUctr,
  output MemtoReg,
  output RegWr,
  output MemWr,
  output [2:0] ExtOp
);

  wire and_3_out, and_4_out, and_5_out, and_6_out, and_7_out, and_8_out, and_9_out, and_10_out, and_11_out,
       and_13_out, and_14_out, and_16_out, and_17_out, and_18_out, and_19_out, not_1_out, not_2_out,
       not_3_out, not_4_out, not_5_out, not_6_out, not_7_out, not_8_out, not_9_out, not_10_out, not_11_out,
       not_12_out, not_13_out, not_14_out, not_15_out, not_16_out, not_17_out, not_18_out, not_19_out,
       not_20_out, not_21_out, not_22_out, not_23_out, not_24_out, not_25_out, not_26_out, not_27_out,
       not_28_out, not_29_out, not_30_out, not_31_out, not_32_out, not_33_out, not_34_out, not_35_out,
       not_36_out, not_37_out, not_38_out, not_39_out, not_40_out, not_41_out, not_42_out, not_43_out,
       not_44_out, not_45_out, not_46_out, not_47_out, not_48_out, not_49_out, not_50_out, not_51_out,
       not_52_out, not_53_out, not_54_out, not_55_out, not_56_out, not_57_out, not_58_out, not_59_out,
       not_60_out, not_61_out, not_62_out, not_63_out, not_64_out, not_65_out;

  not not_1 (not_1_out, op[2]);
  not not_2 (not_2_out, op[3]);
  not not_3 (not_3_out, op[4]);
  and and_1 (Branch, op[6], op[5], not_3_out, not_2_out, not_1_out, op[1], op[0]);
  not not_4 (not_4_out, op[4]);
  and and_2 (ALUASrs, op[6], op[5], not_4_out, op[3], op[2], op[1], op[0]);
  not not_5 (not_5_out, op[3]);
  not not_6 (not_6_out, op[5]);
  not not_7 (not_7_out, op[6]);
  and and_3 (and_3_out, not_7_out, not_6_out, op[4], not_5_out, not_8_out);
  not not_8 (not_8_out, op[2]);
  not not_9 (not_9_out, op[6]);
  not not_10 (not_10_out, op[6]);
  not not_11 (not_11_out, op[3]);
  not not_12 (not_12_out, op[5]);
  and and_4 (and_4_out, not_10_out, op[5], op[4], not_11_out, op[2]);
  or or_1 (ALUBSrc[1], and_3_out, and_4_out, and_6_out, and_5_out);
  not not_13 (not_13_out, op[4]);
  not not_14 (not_14_out, op[3]);
  not not_15 (not_15_out, op[4]);
  not not_16 (not_16_out, op[3]);
  not not_17 (not_17_out, op[6]);
  not not_18 (not_18_out, op[2]);
  not not_19 (not_19_out, op[2]);
  and and_5 (and_5_out, not_17_out, op[5], not_13_out, not_14_out, not_19_out);
  and and_6 (and_6_out, not_9_out, not_12_out, not_15_out, not_16_out, not_18_out);
  not not_20 (not_20_out, op[6]);
  not not_21 (not_21_out, op[3]);
  and and_7 (and_7_out, not_20_out, op[5], op[4], not_21_out, op[2]);
  or or_2 (ALUctr[3], and_7_out, and_8_out);
  not not_22 (not_22_out, op[2]);
  not not_23 (not_23_out, op[6]);
  not not_24 (not_24_out, op[3]);
  not not_25 (not_25_out, op[5]);
  not not_26 (not_26_out, op[4]);
  and and_8 (and_8_out, op[6], op[5], not_26_out, not_24_out, not_22_out);
  and and_9 (and_9_out, not_23_out, not_25_out, op[4], not_29_out, not_30_out);
  or or_3 (ALUctr[2], and_7_out, and_9_out);
  not not_27 (not_27_out, op[3]);
  not not_28 (not_28_out, op[6]);
  not not_29 (not_29_out, op[3]);
  not not_30 (not_30_out, op[2]);
  and and_10 (and_10_out, not_28_out, op[5], op[4], not_27_out, not_31_out, not_33_out, funct3[1], not_32_out);
  or or_4 (ALUctr[1], and_7_out, and_9_out, and_10_out, and_11_out);
  not not_31 (not_31_out, op[2]);
  not not_32 (not_32_out, funct3[0]);
  not not_33 (not_33_out, funct3[2]);
  not not_34 (not_34_out, op[3]);
  not not_35 (not_35_out, op[6]);
  or or_5 (ALUctr[0], and_7_out, and_11_out);
  not not_36 (not_36_out, op[2]);
  not not_37 (not_37_out, funct3[2]);
  and and_11 (and_11_out, not_35_out, op[5], op[4], not_34_out, not_36_out, not_37_out, funct3[1], funct3[0]);
  not not_38 (not_38_out, op[4]);
  not not_39 (not_39_out, op[6]);
  not not_40 (not_40_out, op[5]);
  and and_12 (MemtoReg, not_39_out, not_40_out, not_38_out, not_46_out, not_45_out);
  not not_41 (not_41_out, op[2]);
  not not_42 (not_42_out, op[3]);
  not not_43 (not_43_out, op[4]);
  not not_44 (not_44_out, op[6]);
  and and_13 (and_13_out, not_44_out, op[5], not_43_out, not_42_out, not_41_out);
  not not_45 (not_45_out, op[2]);
  not not_46 (not_46_out, op[3]);
  nor nor_1 (RegWr, and_13_out, and_14_out);
  not not_47 (not_47_out, op[4]);
  not not_48 (not_48_out, op[2]);
  not not_49 (not_49_out, op[3]);
  and and_14 (and_14_out, op[6], op[5], not_47_out, not_49_out, not_48_out);
  not not_50 (not_50_out, op[6]);
  not not_51 (not_51_out, op[3]);
  not not_52 (not_52_out, op[4]);
  and and_15 (MemWr, not_50_out, op[5], not_52_out, not_51_out, not_57_out);
  not not_53 (not_53_out, op[3]);
  not not_54 (not_54_out, op[6]);
  not not_55 (not_55_out, op[2]);
  not not_56 (not_56_out, op[4]);
  and and_16 (and_16_out, not_54_out, op[5], not_56_out, not_53_out, not_55_out);
  not not_57 (not_57_out, op[2]);
  or or_6 (ExtOp[1], and_16_out, and_17_out);
  not not_58 (not_58_out, op[4]);
  not not_59 (not_59_out, op[3]);
  not not_60 (not_60_out, op[6]);
  not not_61 (not_61_out, op[3]);
  not not_62 (not_62_out, op[2]);
  and and_17 (and_17_out, op[6], op[5], not_58_out, not_59_out, not_62_out);
  and and_18 (and_18_out, not_60_out, op[5], op[4], not_61_out, op[2]);
  not not_63 (not_63_out, op[4]);
  not not_64 (not_64_out, op[3]);
  not not_65 (not_65_out, op[2]);
  and and_19 (and_19_out, op[6], op[5], not_63_out, not_64_out, not_65_out);
  or or_7 (ExtOp[0], and_18_out, and_19_out);

  assign ALUBSrc[0] = ALUASrs;
  assign ExtOp[2] = ALUASrs;
  assign Jump = ALUASrs;
endmodule
